# Fritzing sketch minion_gooly_eye_clock (saved by Fritzing 0.9.2b)
breadboards: 1

parts:
  Part1 = Arduino Uno (Rev3) - ICSP  # not connected
  Part2 = Adafruit Motor/Stepper/Servo Shield [part_number="Adafruit #1438"]
  S1 = Momentary Switch [package=ksa_sealed_tac_switch]
  S2 = Momentary Switch [package=ksa_sealed_tac_switch]
  S3 = Momentary Switch [package=ksa_sealed_tac_switch]
  M1 = Stepper Motor - Bipolar
  M2 = Stepper Motor - Bipolar

nets:
  N1: Part2.M2A, M2.A
  N2: Part2.M2B, M2.C
  N3: Part2.M1B, M2.B
  N4: Part2.M1A, M2.D
  N5: Part2.M3A, M1.D
  N6: Part2.M3B, M1.B
  N7: Part2.M4B, M1.C
  N8: Part2.D2, S3.1
  N9: Part2.D3, S2.1
  N10: Part2.D4, S1.1
  N11: Part2.GND, S1.3, S2.3, S3.3

notes:
  Hours
  Minutes
  Googly

custom parts:
  Adafruit Motor/Stepper/Servo Shield: The original Adafruit Motorshield kit is one of our most beloved kits, which is why we decided to make something even better. We have upgraded the shield kit to make the bestest, easiest way to drive DC and Stepper motors. This shield will make quick work of your next robotics project! We kept the ability to drive up to 4 DC motors or 2 stepper motors, but added many improvements: Instead of a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
